# Fritzing sketch PumpControlShield (saved by Fritzing 0.9.2b)
breadboards: 1

parts:
  Q1 = TRANSISTOR_NPN [package=to-92]
  Q2 = TRANSISTOR_NPN [package=to-92]
  LED1 = smd LED [color="Red (633nm)" package="0603 [SMD]"]
  LED2 = smd LED [color="Red (633nm)" package="0603 [SMD]"]
  R1 = Resistor [tolerance=±5% resistance=220 package="2010 [SMD]"]
  R2 = Resistor [tolerance=±5% resistance=220 package="2010 [SMD]"]
  Part1 = Arduino Uno (Rev3) - ICSP
  U1 = RELAY [package=relay-g5q]

nets:
  N1: Q1.E, LED2.anode, Part1.D2
  N2: Q1.C, Q2.C, Part1.5V
  N3: Q2.E, LED1.anode, Part1.D3_PWM
  N4: LED1.cathode, R2.Pin_1
  N5: LED2.cathode, R1.Pin_1
  N6: R1.Pin_0, R2.Pin_0, Part1.GND, U1.COIL2
  N7: Part1.D8, U1.COIL1

notes:
  High water mark
  Low water mark
  120VAC Hot (black wire)
